# Fritzing sketch Insect Robot (saved by Fritzing 0.9.2b)

parts:
  元件1 = Arduino Nano (Rev3.0)
  J1 = Basic Servo
  J2 = Basic Servo
  J3 = Infrared Proximity Sensor
  U1 = LIPO-110mAh [package=lipo-110]  # not connected

nets:
  GND: 元件1.GND, J2.gnd
  N1: 元件1.D12/MISO, J1.pulse
  5V: 元件1.5V, J3.Vcc
  N2: 元件1.A1, J3.Vout
  N3: 元件1.D13/SCK, J2.pulse
