# Fritzing sketch Servo Motor (saved by Fritzing 0.9.3b)
breadboards: 1

parts:
  元件1 = Arduino Nano (Rev3.0)
  R1 = Rotary Potentiometer (Small) [maximum_resistance=100kΩ package=THT]
  J1 = Basic Servo

nets:
  N1: 元件1.D7, J1.pulse
  GND: 元件1.GND, R1.leg1, J1.gnd
  5V: 元件1.5V, R1.leg2, J1.vcc
  N2: 元件1.A0, R1.wiper
